// Logisim project test.circ as structural Verilog: 1 circuit, main circuit main
module main (
  input  in_1,
  input  in_2,
  input  in_3,
  input  in_4,
  input  in_5,
  input  in_6
);

  wire n7447_1_pin9, n7447_1_pin10, n7447_1_pin11, n7447_1_pin12, n7447_1_pin13, n7447_1_pin14,
       n7447_1_pin15, not_1_out, not_2_out, not_3_out, not_4_out, not_5_out, not_6_out, not_7_out, or_1_out,
       or_2_out, or_3_out;

  or or_1 (or_1_out, in_1, in_3, in_5);
  or or_2 (or_2_out, in_2, in_3, in_6);
  or or_3 (or_3_out, in_4, in_5, in_6);
  _7447 u_7447_1 (
    .pin1(or_2_out), .pin2(or_3_out), .pin7(or_1_out), .pin15(n7447_1_pin15), .pin14(n7447_1_pin14),
    .pin13(n7447_1_pin13), .pin12(n7447_1_pin12), .pin11(n7447_1_pin11), .pin10(n7447_1_pin10),
    .pin9(n7447_1_pin9));  // open: pin3, pin4, pin5, pin6
  not not_1 (not_1_out, n7447_1_pin15);
  not not_2 (not_2_out, n7447_1_pin14);
  not not_3 (not_3_out, n7447_1_pin13);
  not not_4 (not_4_out, n7447_1_pin12);
  not not_5 (not_5_out, n7447_1_pin11);
  not not_6 (not_6_out, n7447_1_pin10);
  not not_7 (not_7_out, n7447_1_pin9);
  _7_Segment_Display u_7_segment_display_1 (
    .g(not_2_out), .f(not_1_out), .a(not_3_out), .b(not_4_out), .e(not_7_out), .d(not_6_out), .c(not_5_out));  // open: dp
endmodule
