// Logisim project io_system.circ as structural Verilog: 3 circuits, main circuit main
// output1
module d_latch (
  input  data,
  input  enable,
  output q,
  output not_q
);

  wire nand_1_out, nand_2_out, not_1_out;

  not not_1 (not_1_out, data);
  nand nand_1 (nand_1_out, data, enable);
  nand nand_2 (nand_2_out, enable, not_1_out);
  nand nand_3 (q, nand_1_out, not_q);
  nand nand_4 (not_q, q, nand_2_out);
endmodule

module main (
  input  in_1,
  input  in_2,
  input  in_3,
  input  in_4,
  input  in_5,
  input  in_6,
  input  in_7,
  input  in_8,
  input  in_9,
  input  in_10,
  input  in_11,
  input  in_12,
  input  in_13,
  input  in_14,
  input  in_15,
  input  in_16,
  input  in_17,
  input  in_18,
  input  in_19,
  input  in_20,
  input  in_21,
  input  in_22,
  input  in_23,
  input  in_24,
  input  in_25,
  input  in_26,
  input  in_27,
  input  in_28
);

  wire and_1_out, and_2_out, bit_extender_4_out, clock_1_out, decoder_1_out2, decoder_1_out5, decoder_2_out0,
       decoder_2_out1, decoder_3_out4, decoder_3_out5, or_1_out, r_ram_out, r_rom_out, register_2_q,
       w_ram_out;
  wire [1:0] bit_extender_2_out;
  wire [2:0] bit_extender_1_out, bit_extender_3_out;
  wire [7:0] controlled_buffer_1_out, ram_1_dout, register_1_q, register_3_q, rom_1_data;

  LED led_1 (.in(controlled_buffer_1_out[0]));
  LED led_2 (.in(controlled_buffer_1_out[1]));
  LED led_3 (.in(controlled_buffer_1_out[2]));
  LED led_4 (.in(controlled_buffer_1_out[3]));
  LED led_5 (.in(controlled_buffer_1_out[4]));
  LED led_6 (.in(controlled_buffer_1_out[5]));
  LED led_7 (.in(controlled_buffer_1_out[6]));
  LED led_8 (.in(controlled_buffer_1_out[7]));
  Clock clock_1 (.out(clock_1_out));
  Bit_Extender #(.in_width(4), .out_width(3)) bit_extender_1 (
    .in({in_17, in_18, in_19, in_20}), .out(bit_extender_1_out));
  Decoder #(.select(3)) decoder_1 (
    .out2(decoder_1_out2), .out5(decoder_1_out5), .sel(bit_extender_1_out));  // open: out0, out1, out3, out4, out6, out7, en
  or or_1 (or_1_out, decoder_1_out2, decoder_1_out5);
  assign controlled_buffer_1_out = or_1_out ? {in_1, in_2, in_3, in_4, in_5, in_6, in_7, in_8} : 8'bz;  // Controlled_Buffer controlled_buffer_1
  ROM rom_1 (.addr({in_9, in_10, in_11, in_12, in_13, in_14, in_15, in_16}), .data(rom_1_data));
  Register register_1 (.D(rom_1_data), .en(r_rom_out), .clk(clock_1_out), .Q(register_1_q));  // open: clr
  and r_rom (r_rom_out, in_20, ~in_19, ~in_18, ~in_17);  // AND_Gate
  assign controlled_buffer_1_out = r_rom_out ? register_1_q : 8'bz;  // Controlled_Buffer controlled_buffer_2
  RAM ram_1 (
    .addr({in_9, in_10, in_11, in_12, in_13, in_14, in_15, in_16}), .we(w_ram_out), .oe(r_ram_out),
    .clk(clock_1_out), .din(controlled_buffer_1_out), .dout(ram_1_dout));
  and w_ram (w_ram_out, ~in_20, in_19, ~in_18, ~in_17);  // AND_Gate
  and r_ram (r_ram_out, in_20, in_19, ~in_18, ~in_17);  // AND_Gate
  assign controlled_buffer_1_out = r_ram_out ? ram_1_dout : 8'bz;  // Controlled_Buffer controlled_buffer_3
  Bit_Extender #(.out_width(2)) bit_extender_2 (
    .in({in_9, in_10, in_11, in_12, in_13, in_14, in_15, in_16}), .out(bit_extender_2_out));
  Bit_Extender #(.in_width(4), .out_width(3)) bit_extender_3 (
    .in({in_17, in_18, in_19, in_20}), .out(bit_extender_3_out));
  Decoder #(.select(2)) decoder_2 (
    .out0(decoder_2_out0), .out1(decoder_2_out1), .sel(bit_extender_2_out));  // open: out2, out3, en
  Decoder #(.select(3)) decoder_3 (
    .out4(decoder_3_out4), .out5(decoder_3_out5), .sel(bit_extender_3_out));  // open: out0, out1, out2, out3, out6, out7, en
  Register #(.width(1)) register_2 (
    .D(bit_extender_4_out), .en(and_1_out), .clk(clock_1_out), .Q(register_2_q));  // open: clr
  Bit_Extender #(.out_width(1), .\type ("zero")) bit_extender_4 (
    .in(controlled_buffer_1_out), .out(bit_extender_4_out));
  and and_1 (and_1_out, decoder_2_out1, decoder_3_out5);
  and and_2 (and_2_out, decoder_2_out0, decoder_3_out4);
  assign controlled_buffer_1_out = and_2_out ? register_3_q : 8'bz;  // Controlled_Buffer controlled_buffer_4
  Register register_3 (
    .D({in_28, in_27, in_26, in_25, in_24, in_23, in_22, in_21}), .en(decoder_2_out0), .clk(clock_1_out),
    .Q(register_3_q));  // open: clr
  LED led_9 (.in(register_2_q));

  // Notes on the sheet:
  //   control bus:
  //   0b0001 - read rom
  //   0b0010 - write ram
  //   0b0011 - read ram
  //   0b0100 - read io
  //   0b0101 - write io
  //   data bus (8 bit)
  //   address bus (8 bit)
  //   control bus (4 bit)
  //   true data bus values
  //   contents of rom_1 (hex, n*v repeats v):
  //   ff 1 2 ee 4 5 6 ee
  //   operations:
  //   read: 1
  //   operations:
  //   write: 2
  //   read: 3
  //   device addr
  //   operations:
  //   read: 4
  //   write: 5
  //   ADC example input
  //   io device 0
  //   read only
  //   actuator example output
  //   io device 1
  //   write only
endmodule

// input1
module d_latch_8_bit (
  input  [7:0] data,
  input  enable,
  output [7:0] q
);

  wire nand_1_out, nand_2_out, nand_3_out, nand_4_out, nand_5_out, nand_6_out, nand_7_out, nand_8_out,
       nand_9_out, nand_10_out, nand_11_out, nand_12_out, nand_13_out, nand_14_out, nand_15_out, nand_16_out,
       nand_18_out, nand_20_out, nand_22_out, nand_24_out, nand_26_out, nand_28_out, nand_30_out,
       nand_32_out, not_1_out, not_2_out, not_3_out, not_4_out, not_5_out, not_6_out, not_7_out, not_8_out;

  nand nand_1 (nand_1_out, data[0], enable);
  nand nand_2 (nand_2_out, enable, not_1_out);
  not not_1 (not_1_out, data[0]);
  nand nand_3 (nand_3_out, data[1], enable);
  nand nand_4 (nand_4_out, enable, not_2_out);
  not not_2 (not_2_out, data[1]);
  nand nand_5 (nand_5_out, data[2], enable);
  nand nand_6 (nand_6_out, enable, not_3_out);
  not not_3 (not_3_out, data[2]);
  nand nand_7 (nand_7_out, data[3], enable);
  nand nand_8 (nand_8_out, enable, not_4_out);
  not not_4 (not_4_out, data[3]);
  nand nand_9 (nand_9_out, data[4], enable);
  nand nand_10 (nand_10_out, enable, not_5_out);
  not not_5 (not_5_out, data[4]);
  nand nand_11 (nand_11_out, data[5], enable);
  nand nand_12 (nand_12_out, enable, not_6_out);
  not not_6 (not_6_out, data[5]);
  nand nand_13 (nand_13_out, data[6], enable);
  nand nand_14 (nand_14_out, enable, not_7_out);
  not not_7 (not_7_out, data[6]);
  nand nand_15 (nand_15_out, data[7], enable);
  nand nand_16 (nand_16_out, enable, not_8_out);
  not not_8 (not_8_out, data[7]);
  nand nand_17 (q[0], nand_1_out, nand_18_out);
  nand nand_18 (nand_18_out, q[0], nand_2_out);
  nand nand_19 (q[1], nand_3_out, nand_20_out);
  nand nand_20 (nand_20_out, q[1], nand_4_out);
  nand nand_21 (q[2], nand_5_out, nand_22_out);
  nand nand_22 (nand_22_out, q[2], nand_6_out);
  nand nand_23 (q[3], nand_7_out, nand_24_out);
  nand nand_24 (nand_24_out, q[3], nand_8_out);
  nand nand_25 (q[4], nand_9_out, nand_26_out);
  nand nand_26 (nand_26_out, q[4], nand_10_out);
  nand nand_27 (q[5], nand_11_out, nand_28_out);
  nand nand_28 (nand_28_out, q[5], nand_12_out);
  nand nand_29 (q[6], nand_13_out, nand_30_out);
  nand nand_30 (nand_30_out, q[6], nand_14_out);
  nand nand_31 (q[7], nand_15_out, nand_32_out);
  nand nand_32 (nand_32_out, q[7], nand_16_out);
endmodule
