// Logisim project comparator.circ as structural Verilog: 1 circuit, main circuit main
module main (
  input  NUMBER_A,
  input  in_2,
  input  in_3,
  input  in_4,
  input  in_5,
  input  in_6,
  input  in_7,
  input  in_8,
  input  in_9,
  input  in_10,
  input  NUMBER_B,
  input  in_12,
  input  in_13,
  input  in_14,
  input  in_15,
  input  in_16,
  input  in_17,
  input  in_18
);

  wire and_1_out, and_2_out, and_3_out, and_4_out, and_5_out, and_6_out, and_7_out, and_8_out, and_9_out,
       and_10_out, and_11_out, and_12_out, and_13_out, and_14_out, and_15_out, and_16_out, and_17_out,
       and_18_out, and_19_out, and_20_out, and_21_out, and_22_out, and_23_out, and_24_out, gr_out, grt_out,
       lst_out, lt_out, not_1_out, not_2_out, not_3_out, not_4_out, not_5_out, not_6_out, not_7_out,
       not_8_out, not_9_out, not_10_out, not_11_out, not_12_out, not_13_out, not_14_out, not_15_out,
       not_16_out, not_17_out, not_18_out, not_19_out, not_20_out, not_21_out, not_22_out, not_23_out,
       not_24_out, not_25_out, not_26_out, not_27_out, not_28_out, not_29_out, or_1_out, xor_1_out,
       xor_2_out, xor_3_out, xor_4_out, xor_5_out, xor_6_out, xor_7_out, xor_8_out, xor_9_out;

  not not_1 (not_1_out, in_7);
  not not_2 (not_2_out, in_4);
  xor xor_1 (xor_1_out, in_4, in_7);
  and gr (gr_out, in_4, not_1_out, xor_1_out);
  and lt (lt_out, not_2_out, in_7, xor_1_out);
  not not_3 (not_3_out, xor_1_out);
  not not_4 (not_4_out, NUMBER_B);
  not not_5 (not_5_out, NUMBER_A);
  xor xor_2 (xor_2_out, NUMBER_A, NUMBER_B);
  not not_6 (not_6_out, in_12);
  not not_7 (not_7_out, in_2);
  xor xor_3 (xor_3_out, in_2, in_12);
  not not_8 (not_8_out, in_13);
  not not_9 (not_9_out, in_3);
  xor xor_4 (xor_4_out, in_3, in_13);
  not not_10 (not_10_out, in_14);
  not not_11 (not_11_out, in_5);
  xor xor_5 (xor_5_out, in_5, in_14);
  not not_12 (not_12_out, in_15);
  not not_13 (not_13_out, in_6);
  xor xor_6 (xor_6_out, in_6, in_15);
  not not_14 (not_14_out, in_16);
  not not_15 (not_15_out, in_8);
  xor xor_7 (xor_7_out, in_8, in_16);
  not not_16 (not_16_out, in_17);
  not not_17 (not_17_out, in_9);
  xor xor_8 (xor_8_out, in_9, in_17);
  not not_18 (not_18_out, in_18);
  not not_19 (not_19_out, in_10);
  xor xor_9 (xor_9_out, in_10, in_18);
  and and_1 (and_1_out, NUMBER_A, not_4_out, xor_2_out);
  and and_2 (and_2_out, not_5_out, NUMBER_B, xor_2_out);
  not not_20 (not_20_out, xor_2_out);
  and and_3 (and_3_out, in_2, not_6_out, xor_3_out);
  and and_4 (and_4_out, not_7_out, in_12, xor_3_out);
  not not_21 (not_21_out, xor_3_out);
  and and_5 (and_5_out, in_3, not_8_out, xor_4_out);
  and and_6 (and_6_out, not_9_out, in_13, xor_4_out);
  not not_22 (not_22_out, xor_4_out);
  and and_7 (and_7_out, in_5, not_10_out, xor_5_out);
  and and_8 (and_8_out, not_11_out, in_14, xor_5_out);
  not not_23 (not_23_out, xor_5_out);
  and and_9 (and_9_out, in_6, not_12_out, xor_6_out);
  and and_10 (and_10_out, not_13_out, in_15, xor_6_out);
  not not_24 (not_24_out, xor_6_out);
  and and_11 (and_11_out, in_8, not_14_out, xor_7_out);
  and and_12 (and_12_out, not_15_out, in_16, xor_7_out);
  not not_25 (not_25_out, xor_7_out);
  and and_13 (and_13_out, in_9, not_16_out, xor_8_out);
  and and_14 (and_14_out, not_17_out, in_17, xor_8_out);
  not not_26 (not_26_out, xor_8_out);
  and and_15 (and_15_out, in_10, not_18_out, xor_9_out);
  and and_16 (and_16_out, not_19_out, in_18, xor_9_out);
  not not_27 (not_27_out, xor_9_out);
  and and_17 (and_17_out, and_1_out, not_21_out, not_22_out, not_23_out, not_24_out, not_25_out, not_26_out, not_27_out);
  and and_18 (and_18_out, and_3_out, not_22_out, not_23_out, not_24_out, not_25_out, not_26_out, not_27_out);
  and and_19 (and_19_out, and_5_out, not_23_out, not_24_out, not_25_out, not_26_out, not_27_out);
  and and_20 (and_20_out, and_7_out, not_24_out, not_25_out, not_26_out, not_27_out);
  and and_21 (and_21_out, and_9_out, not_25_out, not_26_out, not_27_out);
  and and_22 (and_22_out, and_11_out, not_26_out, not_27_out);
  and and_23 (and_23_out, and_13_out, not_27_out);
  or or_1 (or_1_out, and_17_out, and_18_out, and_19_out, and_20_out, and_21_out, and_22_out, and_23_out, and_15_out);
  and and_24 (and_24_out, not_20_out, not_21_out, not_22_out, not_23_out, not_24_out, not_25_out, not_26_out, not_27_out);
  not not_28 (not_28_out, and_24_out);
  and lst (lst_out, not_28_out, not_29_out);
  not not_29 (not_29_out, or_1_out);
  and grt (grt_out, not_28_out, or_1_out);
  LED led_1 (.in(and_24_out));
  LED led_2 (.in(lst_out));
  LED led_3 (.in(grt_out));

  // Notes on the sheet:
  //   a b -> gt lt eq
  //   0 0 -> 0 0 1
  //   0 1 -> 0 1 0
  //   1 0 -> 1 0 0
  //   1 1 -> 0 0 1
  //   eq
  //   8-bit (a0->a7 from top)
  //   8-bit (a0->a7 from top)
  //   FULL COMPARATOR
  //   eq
endmodule
